# Fritzing sketch schema_platine (saved by Fritzing 0.9.3b)
breadboards: 1

parts:
  Composant1 = Arduino Nano (Rev3.0)
  Composant3 = LED Matrix - Serial Interface - Red/Green/Blue  # not connected
  Composant2 = LED Matrix - Serial Interface - Red/Green/Blue
  Composant4 = LED Matrix - Serial Interface - Red/Green/Blue  # not connected
  Composant5 = LED Matrix - Serial Interface - Red/Green/Blue  # not connected

nets:
  N1: Composant1.GND, Composant2.SCK

notes:
  GND
